# Fritzing sketch servo_button (saved by Fritzing 0.9.2b)
breadboards: 1

parts:
  Parte1 = Arduino Uno (Rev3)
  S1 = Pushbutton [package="[THT]"]
  S2 = Pushbutton [package="[THT]"]
  S3 = Pushbutton [package="[THT]"]
  R1 = Resistor [tolerance=±5% resistance=10k package=THT]
  R2 = Resistor [tolerance=±5% resistance=10k package=THT]
  R3 = Resistor [tolerance=±5% resistance=10k package=THT]
  J1 = Basic Servo
  C1 = Electrolytic Capacitor [capacitance=1µF package="100 mil [THT, electrolytic]"]

nets:
  N1: Parte1.D3_PWM, S1.Pin_3, S1.Pin_4, R3.Pin_1
  N2: Parte1.D4, S2.Pin_3, S2.Pin_4, R2.Pin_1
  N3: Parte1.D5_PWM, S3.Pin_3, S3.Pin_4, R1.Pin_1
  5V: Parte1.5V, S1.Pin_1, S1.Pin_2, S2.Pin_1, S2.Pin_2, S3.Pin_1, S3.Pin_2, J1.vcc, C1.+
  GND: Parte1.GND, R1.Pin_0, R2.Pin_0, R3.Pin_0, J1.gnd, C1.-
