# Fritzing sketch tank (saved by Fritzing 0.9.2b)
circuit board: 6.88566cm x 5.36311cm
breadboards: 1

parts:
  TA7291P1 = TA7291P [package=HSIP10-P-2.54(THT)]
  M1 = DC Motor
  R1 = Resistor [tolerance=±5% resistance=10k package=THT]
  TA7291P2 = TA7291P [package=HSIP10-P-2.54(THT)]
  R2 = Resistor [tolerance=±5% resistance=10k package=THT]
  M2 = DC Motor
  SBDBT_R = FTDI_BASIC [package=ftdi_basic]
  SBDBT_L = FTDI_BASIC [package=ftdi_basic]
  3_3REG = Voltage Regulator - 3.3V [package="TO220 [THT]"]
  C1 = Ceramic Capacitor [capacitance=100nF package="100 mil [THT, multilayer]"]
  C2 = Capacitor Polarized [package=cpol-radial-10uf-25v]
  パーツ1 = Arduino Uno (Rev3)
  Vcc = Screw terminal - 2 pins [package=THT]

nets:
  GND: TA7291P1.GND, TA7291P2.GND, SBDBT_L.3, 3_3REG.GND, C1.1, C2.-, パーツ1.GND, Vcc.pin1
  N1: TA7291P1.OUT1, M1.pin_1
  N2: TA7291P1.Vref, R1.Pin_0
  N3: TA7291P1.IN1, パーツ1.D3_PWM
  N4: TA7291P1.IN2, パーツ1.D5_PWM
  N5: TA7291P1.Vcc, R1.Pin_1
  N6: TA7291P1.Vs, TA7291P2.Vs, パーツ1.5V, Vcc.pin2
  N7: TA7291P1.OUT2, M1.pin_2
  N8: TA7291P2.OUT1, M2.pin_1
  N9: TA7291P2.Vref, R2.Pin_0
  N10: TA7291P2.IN1, パーツ1.D10_PWM/SS
  N11: TA7291P2.IN2, パーツ1.D11_PWM/MOSI
  N12: TA7291P2.Vcc, R2.Pin_1
  N13: TA7291P2.OUT2, M2.pin_2
  N14: SBDBT_R.5, SBDBT_R.2
  N15: SBDBT_R.1, パーツ1.D12/MISO
  N16: SBDBT_R.3, パーツ1.D7
  N17: SBDBT_R.4, パーツ1.D6_PWM
  N18: SBDBT_L.4, 3_3REG.output_voltage, C2.+
  N19: 3_3REG.input_voltage, C1.0, パーツ1.VIN

custom parts:
  TA7291P: The IC are Full-Bridge Driver. 4 modes available (CW / CCW / STOP / BRAKE) and PWM control. Output current:1.0 A (AVE.) 2.0 A (PEAK)
